# Fritzing sketch ProjetoArduinoTCC (saved by Fritzing 0.9.0b)
breadboards: 1

parts:
  RE1 = Rotary Encoder [package=THT]
  LED1 = LED - 5mm [color="Red (633nm)" package="5 mm [THT]"]
  LED2 = LED - 5mm [color="Yellow (595nm)" package="5 mm [THT]"]
  LED3 = LED - 5mm [color="Green (570nm)" package="5 mm [THT]"]
  R1 = Resistor [tolerance=±5% resistance=220 package=THT]
  R2 = Resistor [tolerance=±5% resistance=220 package=THT]
  R3 = Resistor [tolerance=±5% resistance=220 package=THT]
  Componente2 = Arduino Uno (Rev3)  # not connected
  R4 = Resistor [tolerance=±5% resistance=220 package=THT]
  LED4 = smd LED [color="Blue (430nm)" package="0603 [SMD]"]
  Componente1 = Arduino Ethernet Shield (Rev3)

nets:
  N1: RE1.EncoderPinA, LED1.cathode, LED2.cathode, LED3.cathode, LED4.cathode, Componente1.GND
  N2: RE1.EncoderPinC, Componente1.A0
  N3: RE1.EncoderPinB, Componente1.5V
  N4: LED1.anode, R1.Pin_0
  N5: LED2.anode, R2.Pin_0
  N6: LED3.anode, R3.Pin_0
  N7: R1.Pin_1, Componente1.D2
  N8: R2.Pin_1, Componente1.PWM_D3
  N9: R3.Pin_1, Componente1.SDCS
  N10: R4.Pin_0, LED4.anode
  N11: R4.Pin_1, Componente1.PWM_D5

notes:
  <- Potenciometro
  Led Vermelho = Server Down
  Led Amarelo = Conectando
  Led Verde = Server Up
  Led Azul = Recebendo e Enviando Dados
